# Fritzing sketch diagram (saved by Fritzing 0.9.5d)
stripboards: 1

parts:
  IC3 = IC, DIP package, 8 pins [chip_label=12F629]
  IC4 = IC, DIP package, 16 pins [chip_label=TC4511BP]
  R0 = Resistor [tolerance=±5% resistance=10k package=THT]
  R2 = Resistor [tolerance=±5% resistance=10k package=THT]
  R1 = Resistor [tolerance=±5% resistance=10k package=THT]
  R10 = Resistor [tolerance=±5% resistance=220 package=THT]
  R4 = Resistor [tolerance=±5% resistance=10k package=THT]
  Rf = Resistor [tolerance=±5% resistance=120 package=THT]
  Rc = Resistor [tolerance=±5% resistance=120 package=THT]
  Rb = Resistor [tolerance=±5% resistance=120 package=THT]
  Ra = Resistor [tolerance=±5% resistance=120 package=THT]
  Rg = Resistor [tolerance=±5% resistance=120 package=THT]
  Re = Resistor [tolerance=±5% resistance=120 package=THT]
  Rd = Resistor [tolerance=±5% resistance=120 package=THT]
  RB = Resistor [tolerance=±5% resistance=36k package=THT]
  Rout = Resistor [tolerance=±5% resistance=10k package=THT]
  Q2 = NPN-Transistor [package="TO92 [THT]"]  # not connected
  REB = Resistor [tolerance=±5% resistance=10k package=THT]
  DI2 = 7 Segment Display

nets:
  N1: IC3.pin1, IC3.pin2, IC3.pin3, IC3.pin4, IC3.pin5, IC3.pin6, IC3.pin7, IC3.pin8, IC4.pin1, IC4.pin2, IC4.pin3, IC4.pin4, IC4.pin5, IC4.pin6, IC4.pin7, IC4.pin8, R0.Pin_0, R0.Pin_1, R2.Pin_0, R2.Pin_1, R1.Pin_0, R1.Pin_1, R10.Pin_0, R4.Pin_0, R4.Pin_1, Rf.Pin_1, Rc.Pin_1, Rb.Pin_1, Ra.Pin_1, Rg.Pin_1, Re.Pin_1, Rd.Pin_1, RB.Pin_0, RB.Pin_1, Rout.Pin_0, Rout.Pin_1, REB.Pin_1, DI2.Segment_E, DI2.Segment_D, DI2.Segment_C, DI2.Segment_DP, DI2.Segment_B, DI2.Segment_A, DI2.Segment_F, DI2.Segment_G
  N2: IC4.pin9, IC4.pin10, IC4.pin11, IC4.pin12, IC4.pin13, IC4.pin14, IC4.pin15, IC4.pin16, R10.Pin_1, Rf.Pin_0, Rc.Pin_0, Rb.Pin_0, Ra.Pin_0, Rg.Pin_0, Re.Pin_0, Rd.Pin_0, REB.Pin_0

notes:
  B
  OUT
  GND
  VDD
  E
  C
  VSS
  センサーは5x5
  電源用コネクタ2x3（端につなげば）
  ライト用コネクタ2x4（端につなげば）
